# Fritzing sketch pcb_acid (saved by Fritzing 1.0.4)
stripboards: 1

parts:
  XIAO_ESP32S3 = XIAO ESP32S3 [package="DIP (Dual Inline) [THT]"]
  R1 = Resistor [tolerance=±5% power=0.25W resistance=10k package=THT]
  AUDIO_IO1 = screw terminal, 5 pins
  J24 = female pin header, 20 pins [form="♀ (female)"]
  J25 = female pin header, 20 pins [form="♀ (female)"]
  Part4 = Adafruit SDIO microSD Breakout  # not connected
  C3 = Ceramic Capacitor [capacitance=0.1µF voltage=35V package="100 mil [THT, multilayer]"]
  J26 = double row male pin header, 8 pins [form="♂ (male)"]
  R2 = Resistor [tolerance=±5% power=0.25W resistance=220 package=THT]
  5V = Screw terminal - 2 pins [package=THT]  # not connected
  VOLTAGE_CONVERTER = male pin header, 3 pins [form="♂ (male)"]
  D1 = Schottky Diode [part_number=1N5817 package="Melf DO-213 AB [SMD]"]
  LED = male pin header, 1 pin [form="♂ (male)"]
  BAT = male pin header, 1 pin [form="♂ (male)"]  # not connected
  BAT_2 = JST-03JQ-BT [part_number=JST-JQ-BT package=THT]

nets:
  N1: XIAO_ESP32S3.D8, R2.Pin_0
  N2: XIAO_ESP32S3.5V, D1.cathode
  N3: R1.Pin_0, J24.pin15, R2.Pin_1
  N4: R1.Pin_1, J25.pin3, C3.1, J26.pin1
  N5: AUDIO_IO1.pin1, J24.pin16
  N6: AUDIO_IO1.pin2, J24.pin17
  N7: AUDIO_IO1.pin3, J24.pin18
  N8: AUDIO_IO1.pin4, J24.pin19
  N9: AUDIO_IO1.pin5, J24.pin20, J25.pin1, C3.0, J26.pin2, VOLTAGE_CONVERTER.pin2, BAT_2.pin1
  N10: J24.pin2, J26.pin6
  N11: J24.pin3, J26.pin8
  N12: J24.pin4, J26.pin7
  N13: J24.pin5, J26.pin4
  N14: J24.pin6, J26.pin5
  N15: J24.pin7, J26.pin3
  N16: J25.pin11, LED.pin1
  N17: VOLTAGE_CONVERTER.pin1, BAT_2.pin3

notes:
  ESP32 pins
  D7 - RX
  D8 - TX
  Daisy pins
  D21 (pin 28) - LED

custom parts:
  XIAO ESP32S3: Seeed Studio XIAO ESP32S3 leverages 240MHz Xtensa 32-bit LX7 dual-core processor, supporting both WiFi and BLE 5.0 wireless connectivities, a 2.4GHz Rod antenna, allows for deep sleep mode with power consumption as low as 14μA while supporting lithium battery charging management. Ideal for the Internet of Things, Smart Homes, Wireless wearable devices, Robotics, etc.
