# Fritzing sketch pcb_roto (saved by Fritzing 1.0.4)
stripboards: 4

parts:
  C1 = Ceramic Capacitor [capacitance=0.1µF voltage=35V package="100 mil [THT, multilayer]"]
  C2 = Electrolytic Capacitor [capacitance=100µF voltage=35V package="100 mil [THT, electrolytic]"]
  Part2 = Adafruit SDIO microSD Breakout  # not connected
  SOM4 = Daisy Seed [chip_label=IC package="DIP (Dual Inline) [THT]"]  # not connected
  XIAO_ESP32S2 = XIAO ESP32S3 [package="DIP (Dual Inline) [THT]"]  # not connected
  J3 = female pin header, 20 pins [form="♀ (female)"]
  J4 = female pin header, 20 pins [form="♀ (female)"]
  J5 = female pin header, 7 pins [form="♀ (female)"]
  J6 = female pin header, 7 pins [form="♀ (female)"]
  R1 = Resistor [tolerance=±5% power=0.25W resistance=10k package=THT]
  AUDIO_IO = screw terminal, 5 pins
  R2 = Resistor [tolerance=±5% power=0.25W resistance=220 package=THT]
  Servo = screw terminal, 3 pins
  LED = Screw terminal - 2 pins [package=THT]
  LASER = Screw terminal - 2 pins [package=THT]
  TOF_sensor = screw terminal, 4 pins
  5V = Screw terminal - 2 pins [package=THT]  # not connected
  SilentStepStick_TMC1 = SilentStepStick TMC2130 [package=SO16]  # not connected
  J22 = female pin header, 8 pins [form="♀ (female)"]
  J21 = female pin header, 8 pins [form="♀ (female)"]
  Motor = screw terminal, 4 pins
  12V = Screw terminal - 2 pins [package=THT]
  C3 = Electrolytic Capacitor [capacitance=470µF voltage=35V package="100 mil [THT, electrolytic]"]
  D1 = Schottky Diode [part_number=1N5817 package="300 mil [THT]"]
  R7 = Resistor upright [tolerance=±5% resistance=220 package=THT]
  R6 = Resistor upright [tolerance=±5% resistance=220 package=THT]
  R3 = Resistor upright [tolerance=±5% resistance=220 package=THT]
  D2 = Schottky Diode [part_number=1N5817 package="300 mil [THT]"]  # not connected
  J23 = double row male pin header, 8 pins [form="♂ (male)"]

nets:
  N1: C1.0, C2.-, J3.pin1, J4.pin20, J5.pin2, AUDIO_IO.pin5, Servo.pin3, LED.pin1, J22.pin8, J23.pin2
  N2: C1.1, J3.pin3, R1.Pin_1, J23.pin1
  N3: C2.+, J3.pin2, J5.pin1, Servo.pin2
  N4: J3.pin17, LASER.pin2
  N5: J4.pin2, J23.pin6
  N6: J4.pin3, J23.pin8
  N7: J4.pin4, J23.pin7
  N8: J4.pin5, J23.pin4
  N9: J4.pin6, J23.pin5
  N10: J4.pin7, J23.pin3
  N11: J4.pin15, R1.Pin_0, R2.Pin_0
  N12: J4.pin16, AUDIO_IO.pin1
  N13: J4.pin17, AUDIO_IO.pin2
  N14: J4.pin18, AUDIO_IO.pin3
  N15: J4.pin19, AUDIO_IO.pin4
  N16: J5.pin3, J22.pin7, D1.anode
  N17: J5.pin4, TOF_sensor.pin4
  N18: J5.pin5, TOF_sensor.pin3
  N19: J5.pin6, R2.Pin_1
  N20: J6.pin1, R6.Pin_1
  N21: J6.pin4, Servo.pin1
  N22: J22.pin1, 12V.pin2, C3.+, D1.cathode
  N23: J22.pin2, 12V.pin1, C3.-
  N24: J22.pin3, Motor.pin4
  N25: J22.pin4, Motor.pin3
  N26: J22.pin5, Motor.pin2
  N27: J22.pin6, Motor.pin1
  N28: J21.pin1, R7.Pin_0
  N29: J21.pin7, R6.Pin_0
  N30: J21.pin8, R3.Pin_0

notes:
  SCL
  SDA
  ESP32 pins
  D0 - STEP
  D1 - DIR
  D2 - EN
  D3 - servo
  D7 - RX
  D8 - TX
  D9 - SDA
  D10 - SCL
  UART
  GND
  Daisy pins
  D15 (22) - LED
  D17 (24) - LASER

custom parts:
  Daisy Seed: Daisy is an embedded platform for music. It features everything you need for creating high fidelity audio hardware devices. Just plug in a USB cable and start making sound! No soldering required.
  XIAO ESP32S3: Seeed Studio XIAO ESP32S3 leverages 240MHz Xtensa 32-bit LX7 dual-core processor, supporting both WiFi and BLE 5.0 wireless connectivities, a 2.4GHz Rod antenna, allows for deep sleep mode with power consumption as low as 14μA while supporting lithium battery charging management. Ideal for the Internet of Things, Smart Homes, Wireless wearable devices, Robotics, etc.
  SilentStepStick TMC2130: The TMC2130 provides an integrated motor driver solution for 3D-Printing, Cameras, Scanners and other automated equipment applications. The device has an integrated microstepping indexer, the sensorless stall detection technology StallGuard2™, the sensorless load dependent current control CoolStep™ and the completely noiseless current control mode StealthChop™ and is intended to drive a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
  Resistor upright: A generic upright standing resistor (0.25W)
